# Fritzing sketch PCB (saved by Fritzing 1.0.2b)
circuit board: 15.5556cm x 10.6893cm
breadboards: 1

parts:
  Joystick = Header 6 [package=molex-1x6-ra]
  Toggles = Header 6 [package=molex-1x6-ra]
  Buttons = Header 6 [package=molex-1x6-ra]
  Engine_Lights = Header 6 [package=molex-1x6-ra]
  Thrusters = Header 6 [package=molex-1x6-ra]
  Display = Header 6 [package=molex-1x6-ra]
  Display_Power = Header 2 [package=molex-1x2_lock]
  Mod1 = Raspberry Pi Pico W
  Part1 = Adafruit Audio FX Mini Sound Board [part_number="Adafruit #2342 and #2220"]
  Part2 = Adafruit PAM8302 [part_number="Adafruit #2130"]
  Speaker = Header 2 [package=molex-1x2_lock]
  Rumbler = Header 2 [package=molex-1x2_lock]
  Mode = Header 4 [package=molex-1x4_lock]
  Status_Lights = Header 4 [package=molex-1x4_lock]
  Aux = Header 4 [package=molex-1x4_lock]
  Alt = Header 4 [package=molex-1x4_lock]
  Fuel = Header 4 [package=molex-1x4_lock]
  Master_Alarm = Header 4 [package=molex-1x4_lock]
  IC1 = MCP23017 I2C I/O Expander
  IC2 = MCP23017 I2C I/O Expander
  R1 = Resistor [tolerance=±5% power=0W resistance=68 package=THT]
  Throttle = Header 4 [package=molex-1x4_lock]
  Power = Header 2 [package=molex-1x2_lock]

nets:
  GND: Joystick.1, Toggles.1, Buttons.1, Display.1, Mod1.pin_3, Mod1.pin_18, Mod1.pin_23, Mod1.pin_33, Mod1.pin_38, Part1.GND, Part1.UG, Part2.GND, Part2.AIN-, Rumbler.2, Mode.1, Alt.2, Fuel.2, Master_Alarm.1, IC1.VSS, IC1.A0, IC1.A1, IC1.A2, IC2.VSS, IC2.A1, IC2.A2, R1.Pin_0, Throttle.3, Power.1
  N1: Joystick.2, IC1.GPA3
  N2: Joystick.3, IC1.GPA4
  N3: Joystick.4, IC1.GPA5
  N4: Joystick.5, IC1.GPA6
  N5: Toggles.2, IC1.GPB1
  N6: Toggles.3, IC1.GPB0
  N7: Toggles.4, IC1.GPB2
  N8: Toggles.5, IC1.GPB3
  N9: Buttons.2, IC1.GPB7
  N10: Buttons.3, IC1.GPB6
  N11: Buttons.4, IC1.GPB5
  N12: Buttons.5, IC1.GPB4
  N13: Engine_Lights.1, Thrusters.1, Status_Lights.1, Aux.1, R1.Pin_1
  N14: Engine_Lights.2, IC2.GPA4
  N15: Engine_Lights.3, IC2.GPA5
  N16: Engine_Lights.4, IC2.GPA6
  N17: Engine_Lights.5, IC2.GPA7
  N18: Engine_Lights.6, IC2.GPB0
  N19: Thrusters.2, IC2.GPB1
  N20: Thrusters.3, IC2.GPB2
  N21: Thrusters.4, IC2.GPB3
  N22: Thrusters.5, IC2.GPB4
  N23: Display.2, Mod1.pin_4
  N24: Display.3, Mod1.pin_5
  N25: Display.4, Mod1.pin_14
  N26: Display.5, Mod1.pin_15
  N27: Display.6, Mod1.pin_16
  VDD: Display_Power.1, Display_Power.2, Mod1.pin_36, Part1.VIN, IC1.VDD, IC1.RESET, IC2.VDD, IC2.A0, IC2.RESET, Throttle.2
  N28: Mod1.pin_6, IC1.SDA, IC2.SDA
  N29: Mod1.pin_7, IC1.SCL, IC2.SCL
  N30: Mod1.pin_10, Part1.RST
  N31: Mod1.pin_11, Part1.RX_5V
  N32: Mod1.pin_12, Part1.TX
  N33: Mod1.pin_19, Fuel.4
  N34: Mod1.pin_20, Fuel.3
  N35: Mod1.pin_24, Alt.4
  N36: Mod1.pin_25, Alt.3
  N37: Mod1.pin_31, Throttle.1
  N38: Mod1.pin_39, Part2.VCC, Alt.1, Fuel.1
  N39: Mod1.pin_40, Power.2
  N40: Part1.R_AC, Part2.AIN+
  N41: Part1.L_AC, Rumbler.1
  N42: Part2.VO+, Speaker.1
  N43: Part2.VO-, Speaker.2
  N44: Mode.2, IC1.GPA0
  N45: Mode.3, IC1.GPA1
  N46: Mode.4, IC1.GPA2
  N47: Status_Lights.2, IC2.GPA1
  N48: Status_Lights.3, IC2.GPA2
  N49: Status_Lights.4, IC2.GPA3
  N50: Aux.2, IC2.GPB5
  N51: Aux.3, IC2.GPB6
  N52: Aux.4, IC2.GPB7
  N53: Master_Alarm.2, IC1.GPA7
  N54: Master_Alarm.3, IC2.GPA0

notes:
  Rocket Control Panel
  By John Jones

custom parts:
  Raspberry Pi Pico W: Raspberry Pi Pico W. Based around the RP2040 microcontroller the Pico W is a low cost microcontroller device bringing Raspberry Pi quality, cost, and easy of use to the microcontroller space. The areas marked KEEPOUT in pcb silkscreen should not have traces running through them to avoid shorts on a soldered in module!
  Adafruit Audio FX Mini Sound Board: Would you like to add audio/sound effects to your next project, without an Arduino+Shield? Or maybe you don't even know how to use microcontrollers, you just want to make a sound play whenever you press a button. What about something that has to be very small and portable? You are probably feeling a little frustrated: it's been very hard to find a simple, low cost audio effects trigger that is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
  Adafruit PAM8302: This super small mono amplifier is surprisingly powerful - able to deliver up to 2.5 Watts into 4-8 ohm impedance speakers. Inside the miniature chip is a class D controller, able to run from 2.0V-5.5VDC. Since the amp is a class D, its very efficient (over 90% efficient when driving an 8Ω speaker at over half a Watt) - making it perfect for portable and battery-powered projects. It has built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
  MCP23017 I2C I/O Expander: The MCP23017 uses two i2c pins (these can be shared with other i2c devices), and in exchange gives you 16 general purpose pins. You can set each of 16 pins to be input, output, input with a pullup or open drain. There's even the ability to get an interrupt via an external pin when any of the inputs change so you don't have to keep polling the chip.
